// Logisim project Computador simulador.circ as structural Verilog
module main (
  input  in_1,
  input  in_2,
  input  in_3
);

  wire ADD, CLK, clock_1_out, EQ, GEQ, GT, JMP, LEQ, LT, MovRxRA, MovRxRy, MUL, not_1_out, RDM, STR, SUB;
  wire [1:0] End_RAM, End_Registrador;
  wire [3:0] CONTROLE;
  wire [4:0] CONTADOR;
  wire [7:0] Input_RAM, RAM, Saida_ROM;

  Clock clock_1 (.out(clock_1_out));
  assign CLK = not_1_out ? clock_1_out : 1'bz;  // Controlled_Buffer controlled_buffer_1
  not not_1 (not_1_out, in_1);
  PC pc_1 (.CONTADOR(CONTADOR), .CLK(CLK), .clear(in_2));
  Register register_1 (.D(Saida_ROM), .Q({CONTROLE, End_Registrador, End_RAM}), .clk(CLK));  // open: en, clr
  // Registrador_de_instrução registrador_de_instrução_1: pin names not known; wires that end beside it: Saida_ROM, CLK, in_3, End_RAM, End_Registrador, CONTROLE
  ROM #(.addrWidth(5)) rom_1 (.addr(CONTADOR), .data(Saida_ROM));  // open: sel
  \Decode_instruções  \decode_instruções_1  (
    .in_1(CONTROLE), .EQ(EQ), .LT(LT), .GT(GT), .LEQ(LEQ), .GEQ(GEQ), .JMP(JMP), .MUL(MUL), .ADD(ADD),
    .SUB(SUB), .MovRxRy(MovRxRy), .MovRxRA(MovRxRA), .RDM(RDM), .STR(STR), .HLT(in_1));
  RAM #(.addrWidth(2), .bus("separate")) ram_1 (
    .addr(End_RAM), .din(Input_RAM), .data(RAM), .str(STR), .clk(CLK), .ld(RDM));  // open: sel, clr
  ULA ula_1 ();  // open: Entrada_Rx, Entrada_Ry, in_5, ADD, SUB, MUL

  // Other names for the same wires on the sheet: HLT = in_1

  // Notes on the sheet:
  //   CONTADOR DE PROGRAMA
  //   Registrador de Instrução 
  //   Memoria de programa
  //   Memoria Dados
  //   DECODIFICADOR DE INSTRUÇÕES 
endmodule

module ULA (
  input  [7:0] Entrada_Rx,
  input  [7:0] Entrada_Ry,
  input  ADD,
  input  SUB,
  input  in_5,
  input  MUL
);

  wire [7:0] adder_1_out, multiplier_1_out, SaidaRx, SaidaRy, subtractor_1_out, undriven;

  Register register_1 (.D(Entrada_Rx), .Q(SaidaRx), .clk(in_5));  // open: en, clr
  Register register_2 (.D(Entrada_Ry), .Q(SaidaRy), .clk(in_5));  // open: en, clr
  Comparator comparator_1 (.a(SaidaRx), .b(SaidaRy));  // open: gt, eq, lt
  Comparator comparator_2 (.a(SaidaRx), .b(SaidaRy));  // open: gt, eq, lt
  Comparator comparator_3 (.a(SaidaRx), .b(SaidaRy));  // open: gt, eq, lt
  Adder adder_1 (.a(SaidaRx), .b(SaidaRy), .out(adder_1_out));  // open: cin, cout
  Subtractor subtractor_1 (.a(SaidaRx), .b(SaidaRy), .out(subtractor_1_out));  // open: bin, bout
  Multiplier multiplier_1 (.a(SaidaRx), .b(SaidaRy), .out(multiplier_1_out));  // open: cin, cout
  Controlled_Buffer #(.width(8)) controlled_buffer_1 (.in(undriven));  // open: out, en
  Controlled_Buffer #(.width(8)) controlled_buffer_2 (.in(adder_1_out), .en(ADD));  // open: out
  Controlled_Buffer #(.width(8)) controlled_buffer_3 (.in(subtractor_1_out), .en(SUB));  // open: out
  Controlled_Buffer #(.width(8)) controlled_buffer_4 (.in(multiplier_1_out), .en(MUL));  // open: out

  // Other names for the same wires on the sheet: clock = in_5
endmodule

module PC (
  input  CLK,
  input  clear,
  output [4:0] CONTADOR
);

  Counter #(.width(5), .max('h1f)) counter_1 (.Q(CONTADOR), .clk(CLK), .clr(clear));  // open: load, D, count, carry
endmodule

module \Registrador_de_instrução  (
  input  [7:0] Instrucao_ROM,
  input  CLK,
  output [1:0] End_RAM,
  output [1:0] \Endereço_Registrador ,
  output [3:0] \Instrução_decodificador 
);

  Register #(.trigger("falling")) register_1 (
    .D(Instrucao_ROM), .Q({\Instrução_decodificador , \Endereço_Registrador , End_RAM}), .clk(CLK));  // open: en, clr

  // Notes on the sheet:
  //   Ex:
  //   ADD RX, RY
  //   Bits mais significativos são da INSTRUÇÃO; do meio Rx, ultimos dois bits Ry
  //   01
  //   1001
  //   10
endmodule

module Banco_de_registradores (
  input  [1:0] in_1
);

  Decoder #(.select(2)) decoder_1 (.sel(in_1));  // open: out0, out1, out2, out3, en
endmodule

module \Decode_instruções  (
  input  [3:0] in_1,
  output EQ,
  output LT,
  output GT,
  output LEQ,
  output GEQ,
  output JMP,
  output MUL,
  output ADD,
  output SUB,
  output MovRxRy,
  output MovRxRA,
  output RDM,
  output STR,
  output HLT
);

  Comparator #(.width(4)) comparator_1 (.a(in_1), .b(4'b0010), .eq(EQ));  // open: gt, lt
  Comparator #(.width(4)) comparator_2 (.a(in_1), .b(4'b0011), .eq(LT));  // open: gt, lt
  Comparator #(.width(4)) comparator_3 (.a(in_1), .b(4'b0100), .eq(GT));  // open: gt, lt
  Comparator #(.width(4)) comparator_4 (.a(in_1), .b(4'b0101), .eq(LEQ));  // open: gt, lt
  Comparator #(.width(4)) comparator_5 (.a(in_1), .b(4'b0110), .eq(GEQ));  // open: gt, lt
  Comparator #(.width(4)) comparator_6 (.a(in_1), .b(4'b0111), .eq(JMP));  // open: gt, lt
  Comparator #(.width(4)) comparator_7 (.a(in_1), .b(4'b1000), .eq(MUL));  // open: gt, lt
  Comparator #(.width(4)) comparator_8 (.a(in_1), .b(4'b1001), .eq(ADD));  // open: gt, lt
  Comparator #(.width(4)) comparator_9 (.a(in_1), .b(4'b1010), .eq(SUB));  // open: gt, lt
  Comparator #(.width(4)) comparator_10 (.a(in_1), .b(4'b1011), .eq(MovRxRy));  // open: gt, lt
  Comparator #(.width(4)) comparator_11 (.a(in_1), .b(4'b1100), .eq(MovRxRA));  // open: gt, lt
  Comparator #(.width(4)) comparator_12 (.a(in_1), .b(4'b1101), .eq(RDM));  // open: gt, lt
  Comparator #(.width(4)) comparator_13 (.a(in_1), .b(4'b1110), .eq(STR));  // open: gt, lt
  Comparator #(.width(4)) comparator_14 (.a(in_1), .b(4'b1111), .eq(HLT));  // open: gt, lt
endmodule
